# Fritzing sketch Schaltplan (saved by Fritzing 0.9.3b)
breadboards: 1

parts:
  MCU1 = Raspberry Pi Zero
  R2 = Resistor [tolerance=±5% resistance=1.5k package=THT]
  R3 = Resistor [tolerance=±5% resistance=220 package=THT]
  R4 = Resistor [tolerance=±5% resistance=10k package=THT]
  Player4 = Round Pushbutton
  Player2 = Round Pushbutton
  Player3 = Round Pushbutton
  R5 = Resistor [tolerance=±5% resistance=220 package=THT]
  R6 = Resistor [tolerance=±5% resistance=220 package=THT]
  Player1 = Round Pushbutton
  Startbutton = Square Pushbutton
  J1 = Piezo Speaker
  U1 = WS2812 RGB LED matrix 1x8
  Grove1 = Grove OLED 128x96

nets:
  VCC: MCU1.pin_1, U1.VCC, Grove1.VCC
  N1: MCU1.pin_2, Player4.leg1, Player2.leg1, Player3.leg1, Player1.leg1, Startbutton.leg1
  N2: MCU1.pin_3, Grove1.SCL
  N3: MCU1.pin_5, Grove1.SDA
  GND: MCU1.pin_6, MCU1.pin_14, MCU1.pin_16, MCU1.pin_39, R2.Pin_0, R3.Pin_0, R4.Pin_0, R4.Pin_1, Player4.leg0, R5.Pin_0, R6.Pin_0, J1.pin1, U1.GND, Grove1.GND
  N4: MCU1.pin_10, MCU1.pin_12, U1.DIN
  N5: MCU1.pin_18, J1.pin2
  N6: MCU1.pin_22, MCU1.pin_24, R2.Pin_1, Player3.leg0
  N7: MCU1.pin_27, MCU1.pin_29, R3.Pin_1, Player2.leg0
  N8: MCU1.pin_31, R5.Pin_1, Player1.leg0
  N9: MCU1.pin_35, MCU1.pin_37, R6.Pin_1, Startbutton.leg0

custom parts:
  WS2812 RGB LED matrix 1x8: WS2812 matrix 1x8
